# Fritzing sketch Input_Board_040 (saved by Fritzing 0.9.6b)
circuit board: 10.67cm x 7.87cm
breadboards: 1

parts:
  IC2 = MCP20017 [part_number=MCP23017 package="DIP (Dual Inline) [THT]"]
  IC1 = MCP20017 [part_number=MCP23017 package="DIP (Dual Inline) [THT]"]
  C1 = Ceramic Capacitor [capacitance=100nF voltage=35V package="100 mil [THT, multilayer]"]
  C2 = Ceramic Capacitor [capacitance=100nF voltage=35V package="100 mil [THT, multilayer]"]
  IC3 = ULN2803A [package=THT]
  IC4 = ULN2803A [package=THT]
  IC5 = ULN2803A [package=THT]
  D2 = 1N4148 [package=1n4148-SMD_1206]
  D15 = 1N4148 [package=1n4148-SMD_1206]
  D13 = 1N4148 [package=1n4148-SMD_1206]
  D11 = 1N4148 [package=1n4148-SMD_1206]
  D9 = 1N4148 [package=1n4148-SMD_1206]
  D7 = 1N4148 [package=1n4148-SMD_1206]
  D5 = 1N4148 [package=1n4148-SMD_1206]
  D3 = 1N4148 [package=1n4148-SMD_1206]
  D1 = 1N4148 [package=1n4148-SMD_1206]
  D4 = 1N4148 [package=1n4148-SMD_1206]
  D6 = 1N4148 [package=1n4148-SMD_1206]
  D8 = 1N4148 [package=1n4148-SMD_1206]
  D10 = 1N4148 [package=1n4148-SMD_1206]
  D12 = 1N4148 [package=1n4148-SMD_1206]
  D14 = 1N4148 [package=1n4148-SMD_1206]
  D16 = 1N4148 [package=1n4148-SMD_1206]
  D32 = 1N4148 [package=1n4148-SMD_1206]
  D30 = 1N4148 [package=1n4148-SMD_1206]
  D28 = 1N4148 [package=1n4148-SMD_1206]
  D26 = 1N4148 [package=1n4148-SMD_1206]
  D24 = 1N4148 [package=1n4148-SMD_1206]
  D22 = 1N4148 [package=1n4148-SMD_1206]
  D20 = 1N4148 [package=1n4148-SMD_1206]
  D18 = 1N4148 [package=1n4148-SMD_1206]
  D17 = 1N4148 [package=1n4148-SMD_1206]
  D19 = 1N4148 [package=1n4148-SMD_1206]
  D21 = 1N4148 [package=1n4148-SMD_1206]
  D23 = 1N4148 [package=1n4148-SMD_1206]
  D25 = 1N4148 [package=1n4148-SMD_1206]
  D27 = 1N4148 [package=1n4148-SMD_1206]
  D29 = 1N4148 [package=1n4148-SMD_1206]
  D31 = 1N4148 [package=1n4148-SMD_1206]
  D48 = 1N4148 [package=1n4148-SMD_1206]
  D46 = 1N4148 [package=1n4148-SMD_1206]
  D44 = 1N4148 [package=1n4148-SMD_1206]
  D42 = 1N4148 [package=1n4148-SMD_1206]
  D40 = 1N4148 [package=1n4148-SMD_1206]
  D38 = 1N4148 [package=1n4148-SMD_1206]
  D36 = 1N4148 [package=1n4148-SMD_1206]
  D34 = 1N4148 [package=1n4148-SMD_1206]
  D33 = 1N4148 [package=1n4148-SMD_1206]
  D35 = 1N4148 [package=1n4148-SMD_1206]
  D37 = 1N4148 [package=1n4148-SMD_1206]
  D39 = 1N4148 [package=1n4148-SMD_1206]
  D41 = 1N4148 [package=1n4148-SMD_1206]
  D43 = 1N4148 [package=1n4148-SMD_1206]
  D45 = 1N4148 [package=1n4148-SMD_1206]
  D47 = 1N4148 [package=1n4148-SMD_1206]
  D50 = 1N4148 [package=1n4148-SMD_1206]
  D52 = 1N4148 [package=1n4148-SMD_1206]
  D54 = 1N4148 [package=1n4148-SMD_1206]
  D56 = 1N4148 [package=1n4148-SMD_1206]
  D58 = 1N4148 [package=1n4148-SMD_1206]
  D60 = 1N4148 [package=1n4148-SMD_1206]
  D62 = 1N4148 [package=1n4148-SMD_1206]
  D64 = 1N4148 [package=1n4148-SMD_1206]
  D49 = 1N4148 [package=1n4148-SMD_1206]
  D51 = 1N4148 [package=1n4148-SMD_1206]
  D53 = 1N4148 [package=1n4148-SMD_1206]
  D55 = 1N4148 [package=1n4148-SMD_1206]
  D57 = 1N4148 [package=1n4148-SMD_1206]
  D63 = 1N4148 [package=1n4148-SMD_1206]
  D61 = 1N4148 [package=1n4148-SMD_1206]
  D59 = 1N4148 [package=1n4148-SMD_1206]
  IC6 = ULN2803A [package=THT]
  J4 = female pin header, 10 pins [form="♀ (female)"]
  J3 = female pin header, 10 pins [form="♀ (female)"]
  J2 = female pin header, 10 pins [form="♀ (female)"]
  J1 = female pin header, 10 pins [form="♀ (female)"]
  J4a = female pin header, 10 pins [form="♀ (female)"]
  J3a = female pin header, 10 pins [form="♀ (female)"]
  J2a = female pin header, 10 pins [form="♀ (female)"]
  J1a = female pin header, 10 pins [form="♀ (female)"]
  J11 = female pin header, 1 pin [form="♀ (female)"]
  J12 = female pin header, 1 pin [form="♀ (female)"]
  J13 = female pin header, 2 pins [form="♀ (female)"]
  J14 = female pin header, 2 pins [form="♀ (female)"]
  J5 = male pin header, 5 pins [form="♂ (male)"]
  J6 = male pin header, 5 pins [form="♂ (male)"]
  R36 = Resistor [tolerance=±5% resistance=10k power=0.25 package="1206 [SMD]"]
  R35 = Resistor [tolerance=±5% resistance=10k power=0.25 package="1206 [SMD]"]
  J19 = female pin header, 3 pins [form="♀ (female)"]
  J20 = female pin header, 3 pins [form="♀ (female)"]
  R37 = Resistor [tolerance=±5% resistance=10k power=0.25 package="1206 [SMD]"]
  R38 = Resistor [tolerance=±5% resistance=10k power=0.25 package="1206 [SMD]"]
  R39 = Resistor [tolerance=±5% resistance=10k power=0.25 package="1206 [SMD]"]
  R40 = Resistor [tolerance=±5% resistance=10k power=0.25 package="1206 [SMD]"]
  R41 = Resistor [tolerance=±5% resistance=10k power=0.25 package="1206 [SMD]"]
  R42 = Resistor [tolerance=±5% resistance=10k power=0.25 package="1206 [SMD]"]
  R44 = Resistor [tolerance=±5% resistance=10k power=0.25 package="1206 [SMD]"]
  R43 = Resistor [tolerance=±5% resistance=10k power=0.25 package="1206 [SMD]"]
  R45 = Resistor [tolerance=±5% resistance=10k power=0.25 package="1206 [SMD]"]
  R46 = Resistor [tolerance=±5% resistance=10k power=0.25 package="1206 [SMD]"]
  R47 = Resistor [tolerance=±5% resistance=10k power=0.25 package="1206 [SMD]"]
  R48 = Resistor [tolerance=±5% resistance=10k power=0.25 package="1206 [SMD]"]
  R49 = Resistor [tolerance=±5% resistance=10k power=0.25 package="1206 [SMD]"]
  R50 = Resistor [tolerance=±5% resistance=10k power=0.25 package="1206 [SMD]"]
  R51 = Resistor [tolerance=±5% resistance=10k power=0.25 package="1206 [SMD]"]
  R52 = Resistor [tolerance=±5% resistance=10k power=0.25 package="1206 [SMD]"]
  R53 = Resistor [tolerance=±5% resistance=10k power=0.25 package="1206 [SMD]"]
  R54 = Resistor [tolerance=±5% resistance=10k power=0.25 package="1206 [SMD]"]
  R55 = Resistor [tolerance=±5% resistance=10k power=0.25 package="1206 [SMD]"]
  R56 = Resistor [tolerance=±5% resistance=10k power=0.25 package="1206 [SMD]"]
  R57 = Resistor [tolerance=±5% resistance=10k power=0.25 package="1206 [SMD]"]
  R58 = Resistor [tolerance=±5% resistance=10k power=0.25 package="1206 [SMD]"]
  R59 = Resistor [tolerance=±5% resistance=10k power=0.25 package="1206 [SMD]"]
  R60 = Resistor [tolerance=±5% resistance=10k power=0.25 package="1206 [SMD]"]
  R61 = Resistor [tolerance=±5% resistance=10k power=0.25 package="1206 [SMD]"]
  R62 = Resistor [tolerance=±5% resistance=10k power=0.25 package="1206 [SMD]"]
  R63 = Resistor [tolerance=±5% resistance=10k power=0.25 package="1206 [SMD]"]
  R64 = Resistor [tolerance=±5% resistance=10k power=0.25 package="1206 [SMD]"]
  R65 = Resistor [tolerance=±5% resistance=10k power=0.25 package="1206 [SMD]"]
  R66 = Resistor [tolerance=±5% resistance=10k power=0.25 package="1206 [SMD]"]
  R67 = Resistor [tolerance=±5% resistance=10k power=0.25 package="1206 [SMD]"]
  R68 = Resistor [tolerance=±5% resistance=10k power=0.25 package="1206 [SMD]"]

nets:
  N1: IC2.GPB0, D50.C, D49.A, IC6.In_8, R68.Pin_1
  N2: IC2.GPB1, D52.C, D51.A, IC6.In_7, R67.Pin_1
  N3: IC2.GPB2, D54.C, D53.A, IC6.In_6, R66.Pin_1
  N4: IC2.GPB3, D56.C, D55.A, IC6.In_5, R65.Pin_1
  N5: IC2.GPB04, D58.C, D57.A, IC6.In_4, R64.Pin_1
  N6: IC2.GPB5, D60.C, D59.A, IC6.In_3, R63.Pin_1
  N7: IC2.GPB6, D62.C, D61.A, IC6.In_2, R62.Pin_1
  N8: IC2.GPB8, D64.C, D63.A, IC6.In_1, R61.Pin_1
  +3V3: IC2.VDD, IC2.A0, IC2.RESET, IC1.VDD, IC1.RESET, C1.0, C2.0, D15.C, D13.C, D11.C, D9.C, D7.C, D5.C, D3.C, D1.C, D17.C, D19.C, D21.C, D23.C, D25.C, D27.C, D29.C, D31.C, D33.C, D35.C, D37.C, D39.C, D41.C, D43.C, D45.C, D47.C, D49.C, D51.C, D53.C, D55.C, D57.C, D63.C, D61.C, D59.C, J14.pin1, J14.pin2, J5.pin3, J6.pin3, R36.Pin_0, R35.Pin_1
  GND: IC2.GND, IC1.GND, IC1.A0, C1.1, C2.1, IC3.0V, IC4.0V, IC5.0V, D2.A, D4.A, D6.A, D8.A, D10.A, D12.A, D14.A, D16.A, D32.A, D30.A, D28.A, D26.A, D24.A, D22.A, D20.A, D18.A, D48.A, D46.A, D44.A, D42.A, D40.A, D38.A, D36.A, D34.A, D50.A, D52.A, D54.A, D56.A, D58.A, D60.A, D62.A, D64.A, IC6.0V, J4.pin10, J3.pin10, J2.pin10, J1.pin10, J4a.pin10, J3a.pin10, J2a.pin10, J1a.pin10, J13.pin1, J13.pin2, J5.pin1, J6.pin1, J19.pin2, J20.pin2
  SCL: IC2.SCL, IC1.SCL, J5.pin4, J6.pin4, R36.Pin_1
  SDA: IC2.SDA, IC1.SDA, J5.pin2, J6.pin2, R35.Pin_0
  A1: IC2.A1, IC1.A1, J12.pin1
  A2: IC2.A2, IC1.A2, J11.pin1
  N9: IC2.GPA0, IC5.In_8, D34.C, D33.A, R60.Pin_1
  N10: IC2.GPA1, IC5.In_7, D36.C, D35.A, R59.Pin_1
  N11: IC2.GPA2, IC5.In_6, D38.C, D37.A, R58.Pin_1
  N12: IC2.GPA3, IC5.In_5, D40.C, D39.A, R57.Pin_1
  N13: IC2.GPA4, IC5.In_4, D42.C, D41.A, R56.Pin_1
  N14: IC2.GPA5, IC5.In_3, D44.C, D43.A, R55.Pin_1
  N15: IC2.GPA6, IC5.In_2, D46.C, D45.A, R54.Pin_1
  N16: IC2.GPA7, IC5.In_1, D48.C, D47.A, R53.Pin_1
  N17: IC1.GPB0, IC4.In_8, D18.C, D17.A, R44.Pin_1
  N18: IC1.GPB1, IC4.In_7, D20.C, D19.A, R43.Pin_1
  N19: IC1.GPB2, IC4.In_6, D22.C, D21.A, R42.Pin_1
  N20: IC1.GPB3, IC4.In_5, D24.C, D23.A, R41.Pin_1
  N21: IC1.GPB04, IC4.In_4, D26.C, D25.A, R40.Pin_1
  N22: IC1.GPB5, IC4.In_3, D28.C, D27.A, R39.Pin_1
  N23: IC1.GPB6, IC4.In_2, D30.C, D29.A, R38.Pin_1
  N24: IC1.GPB8, IC4.In_1, D32.C, D31.A, R37.Pin_1
  N25: IC1.GPA0, IC3.In_8, D2.C, D1.A, R52.Pin_1
  N26: IC1.GPA1, IC3.In_7, D3.A, D4.C, R51.Pin_1
  N27: IC1.GPA2, IC3.In_6, D5.A, D6.C, R50.Pin_1
  N28: IC1.GPA3, IC3.In_5, D7.A, D8.C, R49.Pin_1
  N29: IC1.GPA4, IC3.In_4, D9.A, D10.C, R48.Pin_1
  N30: IC1.GPA5, IC3.In_3, D11.A, D12.C, R47.Pin_1
  N31: IC1.GPA6, IC3.In_2, D13.A, D14.C, R46.Pin_1
  N32: IC1.GPA7, IC3.In_1, D15.A, D16.C, R45.Pin_1
  N33: IC3.COM_-_Common, J1.pin1, J1a.pin1, J19.pin1
  N34: IC3.Out_8, J1.pin2, J1a.pin2, R52.Pin_0
  N35: IC3.Out_7, J1.pin3, J1a.pin3, R51.Pin_0
  N36: IC3.Out_6, J1.pin4, J1a.pin4, R50.Pin_0
  N37: IC3.Out_5, J1.pin5, J1a.pin5, R49.Pin_0
  N38: IC3.Out_4, J1.pin6, J1a.pin6, R48.Pin_0
  N39: IC3.Out_3, J1.pin7, J1a.pin7, R47.Pin_0
  N40: IC3.Out_2, J1.pin8, J1a.pin8, R46.Pin_0
  N41: IC3.Out_1, J1.pin9, J1a.pin9, R45.Pin_0
  N42: IC4.COM_-_Common, J2.pin1, J2a.pin1, J19.pin3
  N43: IC4.Out_8, J2.pin2, J2a.pin2, R44.Pin_0
  N44: IC4.Out_7, J2.pin3, J2a.pin3, R43.Pin_0
  N45: IC4.Out_6, J2.pin4, J2a.pin4, R42.Pin_0
  N46: IC4.Out_5, J2.pin5, J2a.pin5, R41.Pin_0
  N47: IC4.Out_4, J2.pin6, J2a.pin6, R40.Pin_0
  N48: IC4.Out_3, J2.pin7, J2a.pin7, R39.Pin_0
  N49: IC4.Out_2, J2.pin8, J2a.pin8, R38.Pin_0
  N50: IC4.Out_1, J2.pin9, J2a.pin9, R37.Pin_0
  N51: IC5.COM_-_Common, J3.pin1, J3a.pin1, J20.pin1
  N52: IC5.Out_8, J3.pin2, J3a.pin2, R60.Pin_0
  N53: IC5.Out_7, J3.pin3, J3a.pin3, R59.Pin_0
  N54: IC5.Out_6, J3.pin4, J3a.pin4, R58.Pin_0
  N55: IC5.Out_5, J3.pin5, J3a.pin5, R57.Pin_0
  N56: IC5.Out_4, J3.pin6, J3a.pin6, R56.Pin_0
  N57: IC5.Out_3, J3.pin7, J3a.pin7, R55.Pin_0
  N58: IC5.Out_2, J3.pin8, J3a.pin8, R54.Pin_0
  N59: IC5.Out_1, J3.pin9, J3a.pin9, R53.Pin_0
  N60: IC6.COM_-_Common, J4.pin1, J4a.pin1, J20.pin3
  N61: IC6.Out_8, J4.pin2, J4a.pin2, R68.Pin_0
  N62: IC6.Out_7, J4.pin3, J4a.pin3, R67.Pin_0
  N63: IC6.Out_6, J4.pin4, J4a.pin4, R66.Pin_0
  N64: IC6.Out_5, J4.pin5, J4a.pin5, R65.Pin_0
  N65: IC6.Out_4, J4.pin6, J4a.pin6, R64.Pin_0
  N66: IC6.Out_3, J4.pin7, J4a.pin7, R63.Pin_0
  N67: IC6.Out_2, J4.pin8, J4a.pin8, R62.Pin_0
  N68: IC6.Out_1, J4.pin9, J4a.pin9, R61.Pin_0
  +24V: J5.pin5, J6.pin5

notes:
  Gnd
  Sda
  +3V3
  Scl
  +24v
  Address Select
  Afkobling
  I2C Bus
  Ano
  Cat
  I/O-PCB  - IHC-Replacement
  V.030 20250322 13:26
  ADDR
  A1
  A2
  v 0.30

custom parts:
  MCP20017: MCP23017, 28 pins on a 300mil dual inline package (DIP) footprint. 16-Bit I/O Expander with I2C Serial Interface
  1N4148: SMD 1206
