# Fritzing sketch Input_Board_020 (saved by Fritzing 0.9.6b)
circuit board: 10cm x 8cm
breadboards: 1

parts:
  IC1 = MCP20017 [part_number=MCP23017 package="DIP (Dual Inline) [THT]"]
  D2 = 1N4148 [package=1n4148-SMD_1206]
  D8 = 1N4148 [package=1n4148-SMD_1206]
  D7 = 1N4148 [package=1n4148-SMD_1206]
  D6 = 1N4148 [package=1n4148-SMD_1206]
  D5 = 1N4148 [package=1n4148-SMD_1206]
  D4 = 1N4148 [package=1n4148-SMD_1206]
  D3 = 1N4148 [package=1n4148-SMD_1206]
  D1 = 1N4148 [package=1n4148-SMD_1206]
  D10 = 1N4148 [package=1n4148-SMD_1206]
  D16 = 1N4148 [package=1n4148-SMD_1206]
  D15 = 1N4148 [package=1n4148-SMD_1206]
  D14 = 1N4148 [package=1n4148-SMD_1206]
  D13 = 1N4148 [package=1n4148-SMD_1206]
  D12 = 1N4148 [package=1n4148-SMD_1206]
  D11 = 1N4148 [package=1n4148-SMD_1206]
  D9 = 1N4148 [package=1n4148-SMD_1206]
  D18 = 1N4148 [package=1n4148-SMD_1206]
  D26 = 1N4148 [package=1n4148-SMD_1206]
  D24 = 1N4148 [package=1n4148-SMD_1206]
  D32 = 1N4148 [package=1n4148-SMD_1206]
  D23 = 1N4148 [package=1n4148-SMD_1206]
  D31 = 1N4148 [package=1n4148-SMD_1206]
  D22 = 1N4148 [package=1n4148-SMD_1206]
  D30 = 1N4148 [package=1n4148-SMD_1206]
  D29 = 1N4148 [package=1n4148-SMD_1206]
  D21 = 1N4148 [package=1n4148-SMD_1206]
  D28 = 1N4148 [package=1n4148-SMD_1206]
  D20 = 1N4148 [package=1n4148-SMD_1206]
  D19 = 1N4148 [package=1n4148-SMD_1206]
  D27 = 1N4148 [package=1n4148-SMD_1206]
  D25 = 1N4148 [package=1n4148-SMD_1206]
  D17 = 1N4148 [package=1n4148-SMD_1206]
  R1 = Resistor [tolerance=±5% power=0.25 resistance=220 package=THT]
  R2 = Resistor [tolerance=±5% power=0.25 resistance=220 package=THT]
  R4 = Resistor [tolerance=±5% power=0.25 resistance=220 package=THT]
  R3 = Resistor [tolerance=±5% power=0.25 resistance=220 package=THT]
  R8 = Resistor [tolerance=±5% power=0.25 resistance=220 package=THT]
  R5 = Resistor [tolerance=±5% power=0.25 resistance=220 package=THT]
  R6 = Resistor [tolerance=±5% power=0.25 resistance=220 package=THT]
  R7 = Resistor [tolerance=±5% power=0.25 resistance=220 package=THT]
  R9 = Resistor [tolerance=±5% power=0.25 resistance=220 package=THT]
  R10 = Resistor [tolerance=±5% power=0.25 resistance=220 package=THT]
  R11 = Resistor [tolerance=±5% power=0.25 resistance=220 package=THT]
  R12 = Resistor [tolerance=±5% power=0.25 resistance=220 package=THT]
  R13 = Resistor [tolerance=±5% power=0.25 resistance=220 package=THT]
  R14 = Resistor [tolerance=±5% power=0.25 resistance=220 package=THT]
  R15 = Resistor [tolerance=±5% power=0.25 resistance=220 package=THT]
  R16 = Resistor [tolerance=±5% power=0.25 resistance=220 package=THT]
  R17 = Resistor [tolerance=±5% resistance=10k power=0.25 package="1206 [SMD]"]
  R18 = Resistor [tolerance=±5% resistance=10k power=0.25 package="1206 [SMD]"]
  J2 = female pin header, 9 pins [form="♀ (female)"]
  J3 = female pin header, 9 pins [form="♀ (female)"]
  J4 = female pin header, 9 pins [form="♀ (female)"]
  J5 = female pin header, 9 pins [form="♀ (female)"]
  J1 = female pin header, 6 pins [form="♀ (female)"]  # not connected
  J6 = female pin header, 2 pins [form="♀ (female)"]  # not connected
  IC2 = MCP20017 [part_number=MCP23017 package="DIP (Dual Inline) [THT]"]
  D33 = 1N4148 [package=1n4148-SMD_1206]
  D34 = 1N4148 [package=1n4148-SMD_1206]
  D35 = 1N4148 [package=1n4148-SMD_1206]
  D36 = 1N4148 [package=1n4148-SMD_1206]
  D37 = 1N4148 [package=1n4148-SMD_1206]
  D38 = 1N4148 [package=1n4148-SMD_1206]
  D39 = 1N4148 [package=1n4148-SMD_1206]
  D40 = 1N4148 [package=1n4148-SMD_1206]
  D41 = 1N4148 [package=1n4148-SMD_1206]
  D42 = 1N4148 [package=1n4148-SMD_1206]
  D43 = 1N4148 [package=1n4148-SMD_1206]
  D44 = 1N4148 [package=1n4148-SMD_1206]
  D45 = 1N4148 [package=1n4148-SMD_1206]
  D46 = 1N4148 [package=1n4148-SMD_1206]
  D47 = 1N4148 [package=1n4148-SMD_1206]
  D48 = 1N4148 [package=1n4148-SMD_1206]
  D49 = 1N4148 [package=1n4148-SMD_1206]
  D50 = 1N4148 [package=1n4148-SMD_1206]
  D51 = 1N4148 [package=1n4148-SMD_1206]
  D52 = 1N4148 [package=1n4148-SMD_1206]
  D53 = 1N4148 [package=1n4148-SMD_1206]
  D54 = 1N4148 [package=1n4148-SMD_1206]
  D55 = 1N4148 [package=1n4148-SMD_1206]
  D56 = 1N4148 [package=1n4148-SMD_1206]
  D57 = 1N4148 [package=1n4148-SMD_1206]
  D58 = 1N4148 [package=1n4148-SMD_1206]
  D59 = 1N4148 [package=1n4148-SMD_1206]
  D60 = 1N4148 [package=1n4148-SMD_1206]
  D61 = 1N4148 [package=1n4148-SMD_1206]
  D62 = 1N4148 [package=1n4148-SMD_1206]
  D63 = 1N4148 [package=1n4148-SMD_1206]
  D64 = 1N4148 [package=1n4148-SMD_1206]
  R19 = Resistor [tolerance=±5% power=0.25 resistance=220 package=THT]
  R20 = Resistor [tolerance=±5% power=0.25 resistance=220 package=THT]
  R21 = Resistor [tolerance=±5% power=0.25 resistance=220 package=THT]
  R22 = Resistor [tolerance=±5% power=0.25 resistance=220 package=THT]
  R23 = Resistor [tolerance=±5% power=0.25 resistance=220 package=THT]
  R24 = Resistor [tolerance=±5% power=0.25 resistance=220 package=THT]
  R25 = Resistor [tolerance=±5% power=0.25 resistance=220 package=THT]
  R26 = Resistor [tolerance=±5% power=0.25 resistance=220 package=THT]
  R27 = Resistor [tolerance=±5% power=0.25 resistance=220 package=THT]
  R28 = Resistor [tolerance=±5% power=0.25 resistance=220 package=THT]
  R29 = Resistor [tolerance=±5% power=0.25 resistance=220 package=THT]
  R30 = Resistor [tolerance=±5% power=0.25 resistance=220 package=THT]
  R31 = Resistor [tolerance=±5% power=0.25 resistance=220 package=THT]
  R32 = Resistor [tolerance=±5% power=0.25 resistance=220 package=THT]
  R33 = Resistor [tolerance=±5% power=0.25 resistance=220 package=THT]
  R34 = Resistor [tolerance=±5% power=0.25 resistance=220 package=THT]
  J7 = female pin header, 9 pins [form="♀ (female)"]
  J8 = female pin header, 9 pins [form="♀ (female)"]
  J9 = female pin header, 9 pins [form="♀ (female)"]
  J10 = female pin header, 9 pins [form="♀ (female)"]
  J11 = female pin header, 3 pins [form="♀ (female)"]  # not connected
  C1 = Ceramic Capacitor [capacitance=100nF voltage=35V package="100 mil [THT, multilayer]"]
  C2 = Ceramic Capacitor [capacitance=100nF voltage=35V package="100 mil [THT, multilayer]"]

nets:
  N1: IC1.GPB0, D8.A, D24.C, R8.Pin_1
  N2: IC1.GPB1, D7.A, D23.C, R7.Pin_1
  N3: IC1.GPB2, D6.A, D22.C, R6.Pin_1
  N4: IC1.GPB3, D5.A, D21.C, R5.Pin_1
  N5: IC1.GPB04, D4.A, D20.C, R4.Pin_1
  N6: IC1.GPB5, D3.A, D19.C, R3.Pin_1
  N7: IC1.GPB6, D2.A, D18.C, R2.Pin_1
  N8: IC1.GPB8, D1.A, D17.C, R1.Pin_1
  N9: IC1.VDD, IC1.A0, IC1.A1, IC1.RESET, D2.C, D8.C, D7.C, D6.C, D5.C, D4.C, D3.C, D1.C, D10.C, D16.C, D15.C, D14.C, D13.C, D12.C, D11.C, D9.C, R17.Pin_1, R18.Pin_1, C2.0
  N10: IC1.GND, C2.1
  N11: IC1.SCL, R17.Pin_0
  N12: IC1.SDA, R18.Pin_0
  N13: IC1.A2, IC2.A2
  N14: IC1.GPA0, D16.A, D32.C, R14.Pin_1
  N15: IC1.GPA1, D15.A, D31.C, R16.Pin_1
  N16: IC1.GPA2, D14.A, D30.C, R10.Pin_1
  N17: IC1.GPA3, D13.A, D29.C, R9.Pin_1
  N18: IC1.GPA4, D12.A, D28.C, R15.Pin_1
  N19: IC1.GPA5, D11.A, D27.C, R13.Pin_1
  N20: IC1.GPA6, D10.A, D26.C, R12.Pin_1
  N21: IC1.GPA7, D9.A, D25.C, R11.Pin_1
  N22: R1.Pin_0, J2.pin9, J3.pin9
  N23: R2.Pin_0, J2.pin8, J3.pin8
  N24: R4.Pin_0, J2.pin6, J3.pin6
  N25: R3.Pin_0, J2.pin7, J3.pin7
  N26: R8.Pin_0, J2.pin2, J3.pin2
  N27: R5.Pin_0, J2.pin5, J3.pin5
  N28: R6.Pin_0, J2.pin4, J3.pin4
  N29: R7.Pin_0, J2.pin3, J3.pin3
  N30: R9.Pin_0, J4.pin5, J5.pin5
  N31: R10.Pin_0, J4.pin4, J5.pin4
  N32: R11.Pin_0, J4.pin9, J5.pin9
  N33: R12.Pin_0, J4.pin8, J5.pin8
  N34: R13.Pin_0, J4.pin7, J5.pin7
  N35: R14.Pin_0, J4.pin2, J5.pin2
  N36: R15.Pin_0, J4.pin6, J5.pin6
  N37: R16.Pin_0, J4.pin3, J5.pin3
  N38: J2.pin1, J3.pin1, J4.pin1, J5.pin1, J7.pin1, J8.pin1, J9.pin1, J10.pin1
  N39: IC2.GPB0, D38.C, D39.A, R23.Pin_1
  N40: IC2.GPB1, D43.A, D44.C, R30.Pin_1
  N41: IC2.GPB2, D45.A, D46.C, R27.Pin_1
  N42: IC2.GPB3, D50.C, D51.A, R26.Pin_1
  N43: IC2.GPB04, D53.A, D54.C, R25.Pin_1
  N44: IC2.GPB5, D59.C, D60.A, R19.Pin_1
  N45: IC2.GPB6, D34.C, D36.A, R31.Pin_1
  N46: IC2.GPB8, D62.A, D63.C, R22.Pin_1
  N47: IC2.VDD, IC2.A1, IC2.RESET, D33.C, D36.C, D37.C, D39.C, D42.C, D43.C, D45.C, D47.C, D51.C, D52.C, D53.C, D55.C, D57.C, D60.C, D61.C, D62.C, C1.0
  N48: IC2.GND, IC2.A0, C1.1
  N49: IC2.GPA0, D37.A, D40.C, R24.Pin_1
  N50: IC2.GPA1, D41.C, D42.A, R32.Pin_1
  N51: IC2.GPA2, D47.A, D48.C, R21.Pin_1
  N52: IC2.GPA3, D49.C, D52.A, R28.Pin_1
  N53: IC2.GPA4, D55.A, D56.C, R29.Pin_1
  N54: IC2.GPA5, D57.A, D58.C, R33.Pin_1
  N55: IC2.GPA6, D33.A, D35.C, R34.Pin_1
  N56: IC2.GPA7, D61.A, D64.C, R20.Pin_1
  N57: R19.Pin_0, J8.pin7, J10.pin7
  N58: R20.Pin_0, J7.pin9, J9.pin9
  N59: R21.Pin_0, J7.pin4, J9.pin4
  N60: R22.Pin_0, J8.pin9, J10.pin9
  N61: R23.Pin_0, J8.pin2, J10.pin2
  N62: R24.Pin_0, J7.pin2, J9.pin2
  N63: R25.Pin_0, J8.pin6, J10.pin6
  N64: R26.Pin_0, J8.pin5, J10.pin5
  N65: R27.Pin_0, J8.pin4, J10.pin4
  N66: R28.Pin_0, J7.pin5, J9.pin5
  N67: R29.Pin_0, J7.pin6, J9.pin6
  N68: R30.Pin_0, J8.pin3, J10.pin3
  N69: R31.Pin_0, J8.pin8, J10.pin8
  N70: R32.Pin_0, J7.pin3, J9.pin3
  N71: R33.Pin_0, J7.pin7, J9.pin7
  N72: R34.Pin_0, J7.pin8, J9.pin8

custom parts:
  MCP20017: MCP23017, 28 pins on a 300mil dual inline package (DIP) footprint. 16-Bit I/O Expander with I2C Serial Interface
  1N4148: SMD 1206
